# Fritzing sketch Pool Sensors Sketch (saved by Fritzing 0.9.5d)
circuit board: 4.5cm x 5.5cm
breadboards: 1

parts:
  S1 = Toggle Switch [package=THT]
  S2 = Toggle Switch [package=THT]
  DS1 = DS18B20 1-Wire Temperature Sensor [part_number=DS18B20]
  U1 = ESP32S-HiLetgo [part_number="NodeMCU ESP-WROOM-32"]
  RHT1 = Humidity and Temperature Sensor RHT03
  R3 = Resistor [tolerance=±5% resistance=220 package=THT]
  R2 = Resistor [tolerance=±5% resistance=1k package=THT]

nets (from the pcb view):
  N1: S1.L1, U1.GPIO23
  N2: S1.COM, S2.COM, R3.Pin_0
  N3: S2.L2, U1.GPIO22
  GND: DS1.GND, U1.GND, RHT1.GND_1, RHT1.GND_2, R3.Pin_1
  N4: DS1.DQ, U1.GPIO21, R2.Pin_0
  VDD: DS1.VDD, U1.3.3, RHT1.Vcc, R2.Pin_1
  N5: U1.GPIO19, RHT1.Data-signal

notes:
  Liquid Level Dual Float Switch
  Pool Temperature DS18B20
  Air Temperature +
  Air Humidity
  AM2302

custom parts:
  ESP32S-HiLetgo: HiLetgo ESP-WROOM-32 ESP32 ESP-32S Development Board 2.4GHz Dual-Mode WiFi + Bluetooth Dual Cores Microcontroller The ESP32 integrated with Antenna switches, RF Balun, power amplifiers, low-noise amplifiers, filters, and management modules, and the entire solution occupies the least area of PCB. 2.4 GHz Wi-Fi plus Bluetooth dual-mode chip, with TSMC Ultra-low power consumption 40nm technology,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
